# Fritzing sketch Elevator_circuit (saved by Fritzing 0.9.3b)
circuit board: 8.46667cm x 5.64444cm
breadboards: 1

parts:
  Part1 = Arduino Uno (Rev3)
  LED_Våning_1 = LED - 5mm [color="Red (633nm)" package="5 mm [THT]"]
  R1 = Resistor [tolerance=±5% resistance=1k package=THT]
  Button_Green = Pushbutton [package="[THT]"]
  Button_Red = Pushbutton [package="[THT]"]
  LED_Våning_2 = LED - 5mm [color="Green (570nm)" package="5 mm [THT]"]
  R2 = Resistor [tolerance=±5% resistance=1k package=THT]
  Button_Blue = Pushbutton [package="[THT]"]
  LED_Våning_3 = LED - 5mm [color="Blue (525nm)" package="5 mm [THT]"]
  R3 = Resistor [tolerance=±5% resistance=1k package=THT]
  R4 = Resistor [tolerance=±5% resistance=10k package=THT]
  R5 = Resistor [tolerance=±5% resistance=10k package=THT]
  R6 = Resistor [tolerance=±5% resistance=10k package=THT]
  Button_hiss_0 = Pushbutton [package="[THT]"]
  R7 = Resistor [tolerance=±5% resistance=10k package=THT]
  R8 = Resistor [tolerance=±5% resistance=10k package=THT]
  R9 = Resistor [tolerance=±5% resistance=10k package=THT]
  Button_hiss_1 = Pushbutton [package="[THT]"]
  Button_hiss_2 = Pushbutton [package="[THT]"]
  Stop = Pushbutton [package="[THT]"]
  sound_signal = Pushbutton [package="[THT]"]
  R11 = Resistor [tolerance=±5% resistance=10k package=THT]
  R12 = Resistor [tolerance=±5% resistance=10k package=THT]
  Q2 = LTR-301 [package=ltr-301]
  R13 = Resistor [tolerance=±5% resistance=33 package=THT]

nets (from the schematic view):
  N1: Part1.A0, Q2.E, R13.Pin_0
  N2: Part1.D8, LED_Våning_3.anode
  N3: Part1.D9_PWM, LED_Våning_2.anode
  N4: Part1.D10_PWM/SS, LED_Våning_1.anode
  N5: Part1.GND, R1.Pin_1, Button_Green.Pin_1, Button_Green.Pin_2, Button_Red.Pin_1, Button_Red.Pin_2, R2.Pin_1, Button_Blue.Pin_1, Button_Blue.Pin_2, R3.Pin_1, Button_hiss_0.Pin_1, Button_hiss_0.Pin_2, Button_hiss_1.Pin_1, Button_hiss_1.Pin_2, Button_hiss_2.Pin_1, Button_hiss_2.Pin_2, Stop.Pin_1, Stop.Pin_2, sound_signal.Pin_1, sound_signal.Pin_2, R13.Pin_1
  N6: Part1.D0/RX, Button_Green.Pin_3, Button_Green.Pin_4, R4.Pin_1
  N7: Part1.D1/TX, Button_Red.Pin_3, Button_Red.Pin_4, R5.Pin_1
  N8: Part1.D2, Button_Blue.Pin_3, Button_Blue.Pin_4, R6.Pin_1
  N9: Part1.D3_PWM, Button_hiss_0.Pin_3, Button_hiss_0.Pin_4, R7.Pin_1
  N10: Part1.D4, R8.Pin_1, Button_hiss_1.Pin_3, Button_hiss_1.Pin_4
  N11: Part1.D5_PWM, R9.Pin_1, Button_hiss_2.Pin_3, Button_hiss_2.Pin_4
  N12: Part1.D6_PWM, Stop.Pin_3, Stop.Pin_4, R11.Pin_1
  N13: Part1.D7, sound_signal.Pin_3, sound_signal.Pin_4, R12.Pin_1
  N14: Part1.5V, R4.Pin_0, R5.Pin_0, R6.Pin_0, R7.Pin_0, R8.Pin_0, R9.Pin_0, R11.Pin_0, R12.Pin_0, Q2.C
  N15: LED_Våning_1.cathode, R1.Pin_0
  N16: LED_Våning_2.cathode, R2.Pin_0
  N17: LED_Våning_3.cathode, R3.Pin_0
